# Fritzing sketch pcb_pump_module (saved by Fritzing 0.9.3b)
perfboards: 1

parts:
  R1 = Resistor [tolerance=±5% resistance=1k package=THT]
  R2 = Resistor [tolerance=±5% resistance=1k package=THT]
  R3 = Resistor [tolerance=±5% resistance=1k package=THT]
  R4 = Resistor [tolerance=±5% resistance=1k package=THT]
  Q1 = NPN-Transistor [package="TO92 [THT]"]
  C1 = Electrolytic Capacitor [capacitance=22µF package="100 mil [THT, electrolytic]"]
  C2 = Ceramic Capacitor [capacitance=100nF package="100 mil [THT, multilayer]"]
  D1 = Rectifier Diode [part_number=1N4001 package="300 mil [THT]"]
  M1 = DC Motor
  Part1 = Arduino Uno (Rev3)
  L1 = Inductor [package="400 mil [THT]"]
  C3 = Electrolytic Capacitor [capacitance=47µF package="100 mil [THT, electrolytic]"]
  R5 = Resistor [tolerance=±5% resistance=2.2k package=THT]

nets:
  N1: R1.Pin_0, R2.Pin_0, R3.Pin_0, R4.Pin_0, L1.pin_1
  5V: R1.Pin_1, R2.Pin_1, R3.Pin_1, R4.Pin_1, Part1.5V
  GND: Q1.E, Part1.GND, C3.-
  N2: Q1.B, R5.Pin_1
  N3: Q1.C, C1.-, C2.0, D1.anode, M1.pin_2
  N4: C1.+, C2.1, D1.cathode, M1.pin_1, L1.pin_0, C3.+
  N5: Part1.D8, R5.Pin_0
